// Logisim project mips.circ as structural Verilog: 5 circuits, main circuit main
module main (
  input  in_1
);

  wire ALUSrc, and_1_out, Branch, clock_1_out, Jump, MemRead, MemToReg, MemWrite, not_1_out, or_1_out,
       RegDst, RegWrite, \Unidade_Lógico_Aritmética_igual ;
  wire [1:0] ALUOp;
  wire [2:0] Controle_da_ULA_ulactrl, multiplexer_1_out, OpCode, rs, rt;
  wire [2:2] rd;
  wire [7:0] adder_1_out, address_Imm, Banco_de_registradores_read_data_1, contRT, multiplexer_2_out,
       multiplexer_3_out, multiplexer_4_out, PC_q, ram_1_data, \Unidade_Lógico_Aritmética_r ;

  Clock clock_1 (.out(clock_1_out));
  Register PC (.D(multiplexer_3_out), .Q(PC_q), .clk(clock_1_out), .clr(in_1));  // open: en
  Adder adder_1 (.a(8'h1), .b(PC_q), .out(adder_1_out));  // open: cin, cout
  ROM #(.dataWidth(18)) rom_1 (.addr(PC_q), .data({OpCode, rs, rt, rd[2], address_Imm}));  // open: sel
  Multiplexer #(.width(3), .enable("false")) multiplexer_1 (
    .in0(rt), .in1({rd[2], address_Imm[7:6]}), .out(multiplexer_1_out), .sel(RegDst));
  Banco_de_registradores Banco_de_registradores (
    .Read_register_1(rs), .Read_register_2(rt), .Write_register(multiplexer_1_out),
    .Write_data(multiplexer_4_out), .RegWrite(RegWrite), .CLOCK(clock_1_out), .CLEAR(in_1),
    .Read_data_1(Banco_de_registradores_read_data_1), .Read_data_2(contRT));
  Multiplexer #(.width(8), .enable("false")) multiplexer_2 (
    .in0(contRT), .in1(address_Imm), .out(multiplexer_2_out), .sel(ALUSrc));
  Unid_de_controle Unidade_de_controle (
    .OpCode(OpCode), .RegDst(RegDst), .RegWrite(RegWrite), .ALUSrc(ALUSrc), .MemWrite(MemWrite),
    .MemRead(MemRead), .MemToReg(MemToReg), .Branch(Branch), .Jump(Jump), .ALUOp(ALUOp));
  Controle_ULA Controle_da_ULA (.funct(address_Imm[2:0]), .ALUOp(ALUOp), .ULACtrl(Controle_da_ULA_ulactrl));
  ULA \Unidade_Lógico_Aritmética  (
    .A(Banco_de_registradores_read_data_1), .B(multiplexer_2_out), .\Operação (Controle_da_ULA_ulactrl),
    .ShiftAmt(address_Imm[5:3]), .R(\Unidade_Lógico_Aritmética_r ), .Igual(\Unidade_Lógico_Aritmética_igual ));
  Multiplexer #(.width(8), .enable("false")) multiplexer_3 (
    .in0(adder_1_out), .in1(address_Imm), .out(multiplexer_3_out), .sel(or_1_out));
  or or_1 (or_1_out, Jump, and_1_out);
  and and_1 (and_1_out, \Unidade_Lógico_Aritmética_igual , Branch);
  not not_1 (not_1_out, clock_1_out);
  RAM #(.bus("separate")) ram_1 (
    .addr(\Unidade_Lógico_Aritmética_r ), .din(contRT), .data(ram_1_data), .str(MemWrite), .clk(not_1_out),
    .ld(MemRead), .clr(in_1));  // open: sel
  Multiplexer #(.width(8), .enable("false")) multiplexer_4 (
    .in0(ram_1_data), .in1(\Unidade_Lógico_Aritmética_r ), .out(multiplexer_4_out), .sel(MemToReg));

  // Other names for the same wires on the sheet: funct[2:0] = address_Imm[2:0]; rd[1:0] = address_Imm[7:6];
  //   ShAmt[2:0] = address_Imm[5:3]

  // Notes on the sheet:
  //   contents of rom_1 (hex, n*v repeats v):
  //   38001 20a08 10a00 20e08 20203 17200 20205 17201 20204 17202 20201 17203 20207 17204 20207 17205
  //   20208 17206 20205 17207 20c00 20800 4a45 1901d 7840 9200 6380 24801 38016 6b83 10c01 3801f
endmodule

// REG
module Banco_de_registradores (
  input  [2:0] Read_register_1,
  input  [2:0] Read_register_2,
  input  [2:0] Write_register,
  input  [7:0] Write_data,
  input  RegWrite,
  input  CLOCK,
  input  CLEAR,
  output [7:0] Read_data_1,
  output [7:0] Read_data_2
);

  wire WEn0, WEn1, WEn2, WEn3, WEn4, WEn5, WEn6, WEn7;
  wire [7:0] Reg0, Reg1, Reg2, Reg3, Reg4, Reg5, Reg6, Reg7, Write0, Write1, Write2, Write3, Write4, Write5,
       Write6, Write7;

  Demultiplexer #(.select(3), .width(8), .enable("false")) demultiplexer_1 (
    .out0(Write0), .out1(Write1), .out2(Write2), .out3(Write3), .out4(Write4), .out5(Write5), .out6(Write6),
    .out7(Write7), .in(Write_data), .sel(Write_register));
  Demultiplexer #(.select(3), .enable("false")) demultiplexer_2 (
    .out0(WEn0), .out1(WEn1), .out2(WEn2), .out3(WEn3), .out4(WEn4), .out5(WEn5), .out6(WEn6), .out7(WEn7),
    .in(RegWrite), .sel(Write_register));
  Register Reg_0 (.D(Write0), .en(WEn0), .Q(Reg0), .clk(CLOCK), .clr(CLEAR));
  Register Reg_1 (.D(Write1), .en(WEn1), .Q(Reg1), .clk(CLOCK), .clr(CLEAR));
  Register Reg_2 (.D(Write2), .en(WEn2), .Q(Reg2), .clk(CLOCK), .clr(CLEAR));
  Register Reg_3 (.D(Write3), .en(WEn3), .Q(Reg3), .clk(CLOCK), .clr(CLEAR));
  Register Reg_4 (.D(Write4), .en(WEn4), .Q(Reg4), .clk(CLOCK), .clr(CLEAR));
  Register Reg_5 (.D(Write5), .en(WEn5), .Q(Reg5), .clk(CLOCK), .clr(CLEAR));
  Register Reg_6 (.D(Write6), .en(WEn6), .Q(Reg6), .clk(CLOCK), .clr(CLEAR));
  Register Reg_7 (.D(Write7), .en(WEn7), .Q(Reg7), .clk(CLOCK), .clr(CLEAR));
  Multiplexer #(.select(3), .width(8), .enable("false")) multiplexer_1 (
    .in0(Reg0), .in1(Reg1), .in2(Reg2), .in3(Reg3), .in4(Reg4), .in5(Reg5), .in6(Reg6), .in7(Reg7),
    .out(Read_data_1), .sel(Read_register_1));
  Multiplexer #(.select(3), .width(8), .enable("false")) multiplexer_2 (
    .in0(Reg0), .in1(Reg1), .in2(Reg2), .in3(Reg3), .in4(Reg4), .in5(Reg5), .in6(Reg6), .in7(Reg7),
    .out(Read_data_2), .sel(Read_register_2));

  // Other names for the same wires on the sheet: Read1[2:0] = Read_register_1; Read2[2:0] = Read_register_2
endmodule

module ULA (
  input  [7:0] A,
  input  [7:0] B,
  input  [2:0] \Operação ,
  input  [2:0] ShiftAmt,
  output [7:0] R,
  output Igual
);

  wire comparator_1_lt;
  wire [7:0] AComp, adder_1_out, ADiv, AMult, ANeg, AShL, AShR, ASub, ASum, BComp, BDiv, bit_extender_1_out,
       BMult, BSub, BSum, divider_1_out, multiplier_1_out, negator_1_out, shifter_1_out, shifter_2_out,
       subtractor_1_out;

  Demultiplexer #(.select(3), .width(8), .enable("false")) demultiplexer_1 (
    .out0(ASum), .out1(ASub), .out2(AMult), .out3(ADiv), .out4(ANeg), .out5(AComp), .out6(AShL), .out7(AShR),
    .in(A), .sel(\Operação ));
  Demultiplexer #(.select(3), .width(8), .enable("false")) demultiplexer_2 (
    .out0(BSum), .out1(BSub), .out2(BMult), .out3(BDiv), .out5(BComp), .in(B), .sel(\Operação ));  // open: out4, out6, out7
  Adder adder_1 (.a(ASum), .b(BSum), .out(adder_1_out));  // open: cin, cout
  Subtractor subtractor_1 (.a(ASub), .b(BSub), .out(subtractor_1_out));  // open: bin, bout
  Multiplier multiplier_1 (.a(AMult), .b(BMult), .out(multiplier_1_out));  // open: cin, cout
  Divider divider_1 (.a(ADiv), .b(BDiv), .out(divider_1_out));  // open: upper, rem
  Negator negator_1 (.in(ANeg), .out(negator_1_out));
  Comparator comparator_1 (.a(AComp), .b(BComp), .eq(Igual), .lt(comparator_1_lt));  // open: gt
  Shifter shifter_1 (.in(AShL), .\dist (ShiftAmt), .out(shifter_1_out));
  Shifter #(.shift("lr")) shifter_2 (.in(AShR), .\dist (ShiftAmt), .out(shifter_2_out));
  assign bit_extender_1_out = {{7{1'b0}}, comparator_1_lt};  // Bit_Extender bit_extender_1
  Multiplexer #(.select(3), .width(8), .enable("false")) multiplexer_1 (
    .in0(adder_1_out), .in1(subtractor_1_out), .in2(multiplier_1_out), .in3(divider_1_out),
    .in4(negator_1_out), .in5(bit_extender_1_out), .in6(shifter_1_out), .in7(shifter_2_out), .out(R),
    .sel(\Operação ));

  // Other names for the same wires on the sheet: Op[2:0] = \Operação 
endmodule

// UC
module Unid_de_controle (
  input  [2:0] OpCode,
  output RegDst,
  output RegWrite,
  output ALUSrc,
  output MemWrite,
  output MemRead,
  output MemToReg,
  output Branch,
  output Jump,
  output [1:0] ALUOp
);

  wire and_1_out, and_4_out, and_5_out, and_8_out, and_9_out, nor_2_out;

  nor nor_1 (RegDst, OpCode[0], OpCode[1], OpCode[2]);
  nor nor_2 (nor_2_out, OpCode[1], OpCode[2]);
  or or_1 (RegWrite, nor_2_out, and_1_out);
  and and_1 (and_1_out, ~OpCode[0], ~OpCode[1], OpCode[2]);  // AND_Gate
  ExactlyOne xor_1 (.out(ALUSrc), .in0(OpCode[0]), .in1(OpCode[1]), .in2(OpCode[2]));
  and and_2 (MemWrite, ~OpCode[0], OpCode[1], ~OpCode[2]);  // AND_Gate
  and and_3 (MemRead, OpCode[0], ~OpCode[1], ~OpCode[2]);  // AND_Gate
  and and_4 (and_4_out, ~OpCode[0], ~OpCode[1], ~OpCode[2]);  // AND_Gate
  or or_2 (MemToReg, and_4_out, and_5_out);
  and and_5 (and_5_out, ~OpCode[0], ~OpCode[1], OpCode[2]);  // AND_Gate
  and and_6 (Branch, OpCode[0], OpCode[1], ~OpCode[2]);  // AND_Gate
  and and_7 (Jump, OpCode[0], OpCode[1], OpCode[2]);
  and and_8 (and_8_out, OpCode[0], OpCode[1], ~OpCode[2]);  // AND_Gate
  or or_3 (ALUOp[0], and_8_out, and_9_out);
  and and_9 (and_9_out, ~OpCode[0], ~OpCode[1], OpCode[2]);  // AND_Gate
  and and_10 (ALUOp[1], ~OpCode[0], ~OpCode[1]);  // AND_Gate
endmodule

module Controle_ULA (
  input  [2:0] funct,
  input  [1:0] ALUOp,
  output [2:0] ULACtrl
);

  Multiplexer #(.select(2), .width(3), .enable("false")) multiplexer_1 (
    .in0(3'b000), .in1(3'b101), .in2(funct), .in3(3'b000), .out(ULACtrl), .sel(ALUOp));
endmodule
